# Fritzing sketch transmitter_schematic (saved by Fritzing 0.9.3b)

parts:
  HC-1 = HC-12 Module
  Componente1 = Arduino Nano (Rev3.0)
  Componente2 = Thumb Joystick

nets:
  N1: HC-1.TXD, Componente1.D10
  N2: HC-1.RXD, Componente1.D11/MOSI
  GND: HC-1.GND, Componente1.GND
  5V: Componente1.5V, Componente2.VCC
  N3: Componente1.A2, Componente2.VERT
  N4: Componente1.A1, Componente2.HORZ
  N5: Componente1.D13/SCK, Componente2.SEL

custom parts:
  HC-12 Module: HC-12 433Mhz Module
